// Logisim project TP10_CheminDonneesMarep.circ as structural Verilog: 2 circuits, main circuit main
module main (
  input  CteOutputXEnable,
  input  RegOutputXEnable,
  input  DTOutputXEnable,
  input  ADOutputXEnable,
  input  RegWriteEnable,
  input  [1:0] NumRegToRead,
  input  DTWriteEnable,
  input  ADWriteEnable,
  input  [1:0] NumRegToWrite,
  input  [3:0] Constante,
  input  ADOutputYEnable,
  input  CteOutputYEnable,
  input  DTOutputYEnable,
  input  ADOutputAddressEnable,
  input  clock,
  input  LoadCommand,
  input  StoreCommand,
  output [3:0] ValeurSurDataIn,
  output [3:0] ValeurSurBusX,
  output [3:0] ValeurSurResOut_DataOut_a56fa60d,
  output [3:0] ValeurSurBusY,
  output [3:0] ValeurSurBusAddress
);

  wire [3:0] banc_registre_1_readvalue, controlled_buffer_4_out, register_1_q, register_2_q;

  assign ValeurSurBusX = CteOutputXEnable ? Constante : 4'bz;  // Controlled_Buffer controlled_buffer_1
  assign ValeurSurBusY = CteOutputYEnable ? Constante : 4'bz;  // Controlled_Buffer controlled_buffer_2
  assign ValeurSurBusX = RegOutputXEnable ? banc_registre_1_readvalue : 4'bz;  // Controlled_Buffer controlled_buffer_3
  assign controlled_buffer_4_out = RegWriteEnable ? ValeurSurResOut_DataOut_a56fa60d : 4'bz;  // Controlled_Buffer controlled_buffer_4
  banc_registre banc_registre_1 (
    .NumReadReg(NumRegToRead), .NumWriteReg(NumRegToWrite), .ValueToWrite(controlled_buffer_4_out),
    .Clock(clock), .ReadValue(banc_registre_1_readvalue));
  Register #(.width(4)) register_1 (
    .D(ValeurSurResOut_DataOut_a56fa60d), .en(ADWriteEnable), .clk(clock), .Q(register_1_q), .clr(1'b0));
  assign ValeurSurBusX = ADOutputXEnable ? register_1_q : 4'bz;  // Controlled_Buffer controlled_buffer_5
  assign ValeurSurBusY = ADOutputYEnable ? register_1_q : 4'bz;  // Controlled_Buffer controlled_buffer_6
  assign ValeurSurBusAddress = ADOutputAddressEnable ? register_1_q : 4'bz;  // Controlled_Buffer controlled_buffer_7
  Register #(.width(4)) register_2 (.D(ValeurSurDataIn), .en(DTWriteEnable), .clk(clock), .Q(register_2_q), .clr(1'b0));
  assign ValeurSurBusX = DTOutputXEnable ? register_2_q : 4'bz;  // Controlled_Buffer controlled_buffer_8
  assign ValeurSurBusY = DTOutputYEnable ? register_2_q : 4'bz;  // Controlled_Buffer controlled_buffer_9
  Adder #(.width(4)) adder_1 (
    .a(ValeurSurBusX), .b(ValeurSurBusY), .out(ValeurSurResOut_DataOut_a56fa60d), .cin(1'b0));  // open: cout
  RAM #(.addrWidth(4), .dataWidth(4)) ram_1 (
    .addr(ValeurSurBusAddress), .we(StoreCommand), .oe(LoadCommand), .clk(clock),
    .din(ValeurSurResOut_DataOut_a56fa60d), .dout(ValeurSurDataIn));

  // Notes on the sheet:
  //   bloc de constantes 4 bits
  //   bus X
  //   bus Y
  //   banc de 4 registres
  //   4 bits
  //   bus ADRESSE
  //   DATA_IN
  //   RES_OUT
  //   ADD
endmodule

// Banc
module banc_registre (
  input  [1:0] NumReadReg,
  input  [3:0] ValueToWrite,
  input  [1:0] NumWriteReg,
  input  Clock,
  output [3:0] ReadValue
);

  wire decoder_1_out0, decoder_1_out1, decoder_1_out2, decoder_1_out3;
  wire [3:0] register_1_q, register_2_q, register_3_q;

  Decoder #(.select(2)) decoder_1 (
    .out0(decoder_1_out0), .out1(decoder_1_out1), .out2(decoder_1_out2), .out3(decoder_1_out3),
    .sel(NumWriteReg), .en(1'b1));
  Register #(.width(4)) register_1 (.D(ValueToWrite), .en(decoder_1_out1), .clk(Clock), .Q(register_1_q), .clr(1'b0));
  Register #(.width(4)) register_2 (.D(ValueToWrite), .en(decoder_1_out2), .clk(Clock), .Q(register_2_q), .clr(1'b0));
  Register #(.width(4)) register_3 (.D(ValueToWrite), .en(decoder_1_out3), .clk(Clock), .Q(register_3_q), .clr(1'b0));
  Multiplexer #(.enable("true"), .select(2), .width(4)) multiplexer_1 (
    .in0(4'b0000), .in1(register_1_q), .in2(register_2_q), .in3(register_3_q), .out(ReadValue),
    .sel(NumReadReg));  // open: en
endmodule
