// Logisim project pgcd_ne_fonctionnant_pas.circ as structural Verilog: 1 circuit, main circuit main
module main (
  input  [3:0] in_1,
  input  [3:0] in_2
);

  wire and_1_out, and_2_out, and_3_out, C0_q, C1_q, C2_q, clock_1_out, comparator_1_eq, comparator_1_gt,
       init_out, nor_1_out, not_1_out, not_2_out, not_3_out, not_4_out, not_5_out, not_6_out, not_7_out,
       not_8_out, not_9_out, not_10_out, not_11_out, not_12_out, not_13_out, or_1_out, or_2_out, or_3_out,
       S1_out, S2_out;
  wire [3:0] a_q, b_q, multiplexer_1_out, multiplexer_2_out, multiplexer_3_out, multiplexer_4_out,
       subtractor_1_out;

  Comparator #(.width(4)) comparator_1 (.a(b_q), .b(a_q), .gt(comparator_1_gt), .eq(comparator_1_eq));  // open: lt
  not not_1 (not_1_out, C1_q);
  not not_2 (not_2_out, comparator_1_gt);
  not not_3 (not_3_out, C2_q);
  not not_4 (not_4_out, C1_q);
  not not_5 (not_5_out, C2_q);
  not not_6 (not_6_out, C1_q);
  not not_7 (not_7_out, comparator_1_eq);
  not not_8 (not_8_out, C2_q);
  Clock clock_1 (.out(clock_1_out));
  and and_1 (and_1_out, not_3_out, not_4_out, C0_q, comparator_1_eq);
  and and_2 (and_2_out, not_5_out, not_6_out, C0_q, not_7_out);
  and and_3 (and_3_out, not_8_out, not_1_out, C0_q, not_2_out);
  // Probe on subtractor_1_out
  Multiplexer #(.width(4)) multiplexer_1 (.in0(subtractor_1_out), .in1(in_1), .out(multiplexer_1_out), .sel(init_out));
  Multiplexer #(.width(4)) multiplexer_2 (.in0(subtractor_1_out), .in1(in_2), .out(multiplexer_2_out), .sel(init_out));
  nor nor_1 (nor_1_out, and_3_out, C2_q);
  or or_1 (or_1_out, S1_out, init_out);
  Register #(.width(1)) C2 (.D(or_2_out), .en(1'b1), .clk(clock_1_out), .Q(C2_q));  // open: clr
  or or_2 (or_2_out, C2_q, and_1_out);
  Register #(.width(1)) C1 (.D(and_2_out), .en(1'b1), .clk(clock_1_out), .Q(C1_q));  // open: clr
  Register #(.width(1)) C0 (.D(nor_1_out), .en(1'b1), .clk(clock_1_out), .Q(C0_q));  // open: clr
  Register #(.width(4)) a (.D(multiplexer_1_out), .en(or_3_out), .clk(clock_1_out), .Q(a_q));  // open: clr
  Register #(.width(4)) b (.D(multiplexer_2_out), .en(or_1_out), .clk(clock_1_out), .Q(b_q));  // open: clr
  not not_9 (not_9_out, C2_q);
  Multiplexer #(.width(4)) multiplexer_3 (.in0(a_q), .in1(b_q), .out(multiplexer_3_out), .sel(S1_out));
  Multiplexer #(.width(4)) multiplexer_4 (.in0(b_q), .in1(a_q), .out(multiplexer_4_out), .sel(S1_out));
  and init (init_out, not_9_out, not_10_out, C0_q);
  not not_10 (not_10_out, C1_q);
  not not_11 (not_11_out, C2_q);
  Subtractor #(.width(4)) subtractor_1 (
    .a(multiplexer_3_out), .b(multiplexer_4_out), .out(subtractor_1_out));  // open: bin, bout
  and S1 (S1_out, not_11_out, C1_q, not_12_out);
  not not_12 (not_12_out, C0_q);
  and S2 (S2_out, not_13_out, C1_q, C0_q);
  not not_13 (not_13_out, C2_q);
  or or_3 (or_3_out, init_out, S2_out);
endmodule
