// Logisim project tme.circ as structural Verilog
module main (
  input  a,
  input  b,
  output out_3
);

  wire and_1_out, and_2_out, not_1_out, not_2_out;

  not not_1 (not_1_out, a);
  not not_2 (not_2_out, b);
  and and_1 (and_1_out, not_1_out, b);
  and and_2 (and_2_out, a, not_2_out);
  or or_1 (out_3, and_1_out, and_2_out);

  // Notes on the sheet:
  //   mon_xor
endmodule

module mux2 (
  input  i,
  input  a,
  input  b,
  output out_4
);

  wire and_1_out, and_2_out, not_1_out;

  not not_1 (not_1_out, i);
  and and_1 (and_1_out, not_1_out, a);
  and and_2 (and_2_out, i, b);
  or or_1 (out_4, and_1_out, and_2_out);
endmodule

module mux4bits (
  input  a0,
  input  b0,
  input  i,
  input  a1,
  input  b1,
  input  a2,
  input  b2,
  input  a3,
  input  b3,
  output s0,
  output s1,
  output s2,
  output s3
);

  mux2 mux2_1 (.i(i), .a(a2), .b(b2), .out_4(s2));
  mux2 mux2_2 (.i(i), .a(a3), .b(b3), .out_4(s3));
  mux2 mux2_3 (.i(i), .a(a0), .b(b0), .out_4(s0));
  mux2 mux2_4 (.i(i), .a(a1), .b(b1), .out_4(s1));
endmodule

module mux4in (
  input  i1,
  input  a,
  input  b,
  input  i0,
  input  c,
  input  d,
  output out_7
);

  wire mux2_1_out_4, mux2_2_out_4;

  mux2 mux2_1 (.i(i0), .a(a), .b(b), .out_4(mux2_1_out_4));
  mux2 mux2_2 (.i(i0), .a(c), .b(d), .out_4(mux2_2_out_4));
  mux2 mux2_3 (.i(i1), .a(mux2_1_out_4), .b(mux2_2_out_4), .out_4(out_7));
endmodule

module add1 (
  input  A,
  input  B,
  input  Cin,
  output Cout,
  output S
);

  wire and_1_out, and_2_out, xor_1_out;

  and and_1 (and_1_out, A, B);
  xor xor_1 (xor_1_out, A, B);
  and and_2 (and_2_out, xor_1_out, Cin);
  xor xor_2 (S, xor_1_out, Cin);
  or or_1 (Cout, and_1_out, and_2_out);
endmodule

module add4 (
  input  B0,
  input  B1,
  input  B2,
  input  B3,
  input  in_5,
  input  A0,
  input  A1,
  input  A2,
  input  A3,
  output CF,
  output OV,
  output S0,
  output S1,
  output S2,
  output S3
);

  wire add1_1_cout, add1_2_cout, add1_3_cout, xor_1_out, xor_2_out, xor_3_out, xor_4_out;

  xor xor_1 (xor_1_out, B0, in_5);
  xor xor_2 (xor_2_out, in_5, B1);
  xor xor_3 (xor_3_out, B2, in_5);
  add1 add1_1 (.A(xor_1_out), .B(A0), .Cin(in_5), .Cout(add1_1_cout), .S(S0));
  add1 add1_2 (.A(xor_2_out), .B(A1), .Cin(add1_1_cout), .Cout(add1_2_cout), .S(S1));
  xor xor_4 (xor_4_out, B3, in_5);
  add1 add1_3 (.A(xor_3_out), .B(A2), .Cin(add1_2_cout), .Cout(add1_3_cout), .S(S2));
  xor xor_5 (OV, CF, add1_3_cout);
  add1 add1_4 (.A(xor_4_out), .B(A3), .Cin(add1_3_cout), .Cout(CF), .S(S3));
endmodule
