// Logisim project tme9.circ as structural Verilog
module main (
  input  [3:0] in_1,
  input  in_2,
  output [3:0] out_3
);

  wire clock_1_out;

  Clock clock_1 (.out(clock_1_out));
  Register #(.width(4)) register_1 (.D(in_1), .en(in_2), .clk(clock_1_out), .Q(out_3), .clr(1'b0));
endmodule

module data (
  input  [3:0] in_1,
  input  in_2,
  input  [3:0] in_3,
  input  in_4,
  input  [3:0] in_5,
  input  in_6,
  input  [3:0] in_7,
  input  in_8,
  input  [1:0] in_9,
  input  [1:0] in_10,
  input  in_11,
  input  in_12,
  input  in_13,
  input  in_14,
  input  in_15,
  output out_16,
  output out_17
);

  wire clock_1_out;
  wire [3:0] multiplexer_1_out, multiplexer_2_out, multiplexer_3_out, multiplexer_4_out, multiplexer_5_out,
       multiplexer_6_out, register_1_q, register_2_q, register_3_q, register_4_q, undriven;

  Multiplexer #(.width(4)) multiplexer_1 (.in0(undriven), .in1(in_5), .out(multiplexer_1_out), .sel(in_6));
  Multiplexer #(.width(4)) multiplexer_2 (.in0(undriven), .in1(in_7), .out(multiplexer_2_out), .sel(in_8));
  Multiplexer #(.width(4)) multiplexer_3 (.in0(undriven), .in1(in_1), .out(multiplexer_3_out), .sel(in_2));
  Multiplexer #(.width(4)) multiplexer_4 (.in0(undriven), .in1(in_3), .out(multiplexer_4_out), .sel(in_4));
  Clock clock_1 (.out(clock_1_out));
  Register #(.width(4)) register_1 (.D(multiplexer_3_out), .en(in_12), .clk(clock_1_out), .Q(register_1_q), .clr(1'b0));
  Register #(.width(4)) register_2 (.D(multiplexer_4_out), .en(in_13), .clk(clock_1_out), .Q(register_2_q), .clr(1'b0));
  Register #(.width(4)) register_3 (.D(multiplexer_1_out), .en(in_14), .clk(clock_1_out), .Q(register_3_q), .clr(1'b0));
  Register #(.width(4)) register_4 (.D(multiplexer_2_out), .en(in_15), .clk(clock_1_out), .Q(register_4_q), .clr(1'b0));
  Multiplexer #(.select(2), .width(4)) multiplexer_5 (
    .in0(register_1_q), .in1(register_2_q), .in2(register_3_q), .in3(register_4_q), .out(multiplexer_5_out),
    .sel(in_9));
  Multiplexer #(.select(2), .width(4)) multiplexer_6 (
    .in0(register_1_q), .in1(register_2_q), .in2(register_3_q), .in3(register_4_q), .out(multiplexer_6_out),
    .sel(in_10));
  add4 add4_1 (
    .B0(multiplexer_5_out[0]), .B1(multiplexer_5_out[1]), .B2(multiplexer_5_out[2]),
    .B3(multiplexer_5_out[3]), .in_5(in_11), .A0(multiplexer_6_out[0]), .A1(multiplexer_6_out[1]),
    .A2(multiplexer_6_out[2]), .A3(multiplexer_6_out[3]), .CF(out_16), .OV(out_17));  // open: S0, S1, S2, S3
endmodule

module mux2 (
  input  i,
  input  a,
  input  b,
  output out_4
);

  wire and_1_out, and_2_out, not_1_out;

  not not_1 (not_1_out, i);
  and and_1 (and_1_out, not_1_out, a);
  and and_2 (and_2_out, i, b);
  or or_1 (out_4, and_1_out, and_2_out);
endmodule

module mux4bits (
  input  a0,
  input  b0,
  input  i,
  input  a1,
  input  b1,
  input  a2,
  input  b2,
  input  a3,
  input  b3,
  output s0,
  output s1,
  output s2,
  output s3
);

  mux2 mux2_1 (.i(i), .a(a2), .b(b2), .out_4(s2));
  mux2 mux2_2 (.i(i), .a(a3), .b(b3), .out_4(s3));
  mux2 mux2_3 (.i(i), .a(a0), .b(b0), .out_4(s0));
  mux2 mux2_4 (.i(i), .a(a1), .b(b1), .out_4(s1));
endmodule

module mux4in (
  input  i1,
  input  a,
  input  b,
  input  i0,
  input  c,
  input  d,
  output out_7
);

  wire mux2_1_out_4, mux2_2_out_4;

  mux2 mux2_1 (.i(i0), .a(a), .b(b), .out_4(mux2_1_out_4));
  mux2 mux2_2 (.i(i0), .a(c), .b(d), .out_4(mux2_2_out_4));
  mux2 mux2_3 (.i(i1), .a(mux2_1_out_4), .b(mux2_2_out_4), .out_4(out_7));
endmodule

module add1 (
  input  A,
  input  B,
  input  Cin,
  output Cout,
  output S
);

  wire and_1_out, and_2_out, xor_1_out;

  and and_1 (and_1_out, A, B);
  xor xor_1 (xor_1_out, A, B);
  and and_2 (and_2_out, xor_1_out, Cin);
  xor xor_2 (S, xor_1_out, Cin);
  or or_1 (Cout, and_1_out, and_2_out);
endmodule

module add4 (
  input  B0,
  input  B1,
  input  B2,
  input  B3,
  input  in_5,
  input  A0,
  input  A1,
  input  A2,
  input  A3,
  output CF,
  output OV,
  output S0,
  output S1,
  output S2,
  output S3
);

  wire add1_1_cout, add1_2_cout, add1_3_cout, xor_1_out, xor_2_out, xor_3_out, xor_4_out;

  xor xor_1 (xor_1_out, B0, in_5);
  xor xor_2 (xor_2_out, in_5, B1);
  xor xor_3 (xor_3_out, B2, in_5);
  add1 add1_1 (.A(xor_1_out), .B(A0), .Cin(in_5), .Cout(add1_1_cout), .S(S0));
  add1 add1_2 (.A(xor_2_out), .B(A1), .Cin(add1_1_cout), .Cout(add1_2_cout), .S(S1));
  xor xor_4 (xor_4_out, B3, in_5);
  add1 add1_3 (.A(xor_3_out), .B(A2), .Cin(add1_2_cout), .Cout(add1_3_cout), .S(S2));
  xor xor_5 (OV, CF, add1_3_cout);
  add1 add1_4 (.A(xor_4_out), .B(A3), .Cin(add1_3_cout), .Cout(CF), .S(S3));
endmodule
